// Logisim project 交通灯信号产生电路_U201610504.circ as structural Verilog: 6 circuits, main circuit 四位二进制带同步加载的可逆计数器
module \四位二进制带同步加载的可逆计数器  (
  input  CP_d,
  input  CP_u,
  input  ld,
  input  clr,
  input  ld_3,
  input  ld_2,
  input  ld_1,
  input  ld_0,
  output QD,
  output QC,
  output QB,
  output QA
);

  wire and_1_out, and_2_out, and_3_out, and_4_out, and_5_out, and_6_out, and_7_out, and_8_out, and_9_out,
       and_10_out, and_11_out, and_12_out, and_13_out, and_14_out, and_15_out, and_16_out, and_17_out,
       and_18_out, D0_qn, D1_qn, D2_qn, not_1_out, or_1_out, or_2_out, or_3_out, or_4_out, or_5_out,
       or_6_out, or_7_out, or_8_out, or_9_out, or_10_out, or_11_out, xor_1_out, xor_2_out, xor_3_out,
       xor_4_out, xor_5_out, xor_6_out;

  and and_1 (and_1_out, QC, QB, QA);
  and and_2 (and_2_out, D2_qn, D1_qn, D0_qn);
  and and_3 (and_3_out, QB, QA);
  and and_4 (and_4_out, D1_qn, D0_qn);
  xor xor_1 (xor_1_out, and_1_out, QD);
  xor xor_2 (xor_2_out, and_2_out, QD);
  xor xor_3 (xor_3_out, and_3_out, QC);
  xor xor_4 (xor_4_out, and_4_out, QC);
  xor xor_5 (xor_5_out, QB, QA);
  xor xor_6 (xor_6_out, D0_qn, QB);
  and and_5 (and_5_out, CP_u, xor_1_out);
  and and_6 (and_6_out, CP_d, xor_2_out);
  and and_7 (and_7_out, CP_u, xor_3_out);
  and and_8 (and_8_out, CP_d, xor_4_out);
  and and_9 (and_9_out, CP_u, xor_5_out);
  and and_10 (and_10_out, CP_d, xor_6_out);
  not not_1 (not_1_out, ld);
  or or_1 (or_1_out, CP_u, ld, CP_d);
  or or_2 (or_2_out, and_5_out, and_6_out);
  or or_3 (or_3_out, CP_u, ld, CP_d);
  or or_4 (or_4_out, and_7_out, and_8_out);
  or or_5 (or_5_out, CP_u, ld, CP_d);
  or or_6 (or_6_out, and_9_out, and_10_out);
  or or_7 (or_7_out, CP_u, ld, CP_d);
  and and_11 (and_11_out, not_1_out, or_2_out);
  and and_12 (and_12_out, ld, ld_3);
  and and_13 (and_13_out, not_1_out, or_4_out);
  and and_14 (and_14_out, ld, ld_2);
  and and_15 (and_15_out, not_1_out, or_6_out);
  and and_16 (and_16_out, ld, ld_1);
  and and_17 (and_17_out, not_1_out, D0_qn);
  and and_18 (and_18_out, ld, ld_0);
  or or_8 (or_8_out, and_11_out, and_12_out);
  or or_9 (or_9_out, and_13_out, and_14_out);
  or or_10 (or_10_out, and_15_out, and_16_out);
  or or_11 (or_11_out, and_17_out, and_18_out);
  D_Flip_Flop #(.trigger("falling")) D3 (.clk(or_1_out), .D(or_8_out), .Q(QD), .reset(clr));  // open: Qn, preset, en
  D_Flip_Flop #(.trigger("falling")) D2 (
    .clk(or_3_out), .D(or_9_out), .Q(QC), .Qn(D2_qn), .reset(clr));  // open: preset, en
  D_Flip_Flop #(.trigger("falling")) D1 (
    .clk(or_5_out), .D(or_10_out), .Q(QB), .Qn(D1_qn), .reset(clr));  // open: preset, en
  D_Flip_Flop #(.trigger("falling")) D0 (
    .clk(or_7_out), .D(or_11_out), .Q(QA), .Qn(D0_qn), .reset(clr));  // open: preset, en
endmodule

module \红绿灯点亮时长计时器  (
  input  clk,
  input  clr,
  input  X0,
  input  X1,
  output change
);

  wire _3s_out, _10s_out, _20s_out, and_1_out, and_2_out, not_1_out, not_2_out, or_1_out, or_2_out,
       \四位二进制带同步加载的可逆计数器_1_qa , \四位二进制带同步加载的可逆计数器_1_qb , \四位二进制带同步加载的可逆计数器_1_qd , \四位二进制带同步加载的可逆计数器_2_qa ,
       \四位二进制带同步加载的可逆计数器_2_qb ;

  not not_1 (not_1_out, X0);
  not not_2 (not_2_out, X1);
  or or_1 (or_1_out, clr, change, and_1_out);
  nand _3s (_3s_out, and_2_out, X0);
  nand _10s (_10s_out, not_1_out, X1, \四位二进制带同步加载的可逆计数器_2_qa );
  nand _20s (_20s_out, not_1_out, \四位二进制带同步加载的可逆计数器_2_qb , not_2_out);
  nand nand_1 (change, _3s_out, _10s_out, _20s_out);
  and and_1 (and_1_out, \四位二进制带同步加载的可逆计数器_1_qd , \四位二进制带同步加载的可逆计数器_1_qb );
  \四位二进制带同步加载的可逆计数器  \u_四位二进制带同步加载的可逆计数器_1  (
    .CP_d(1'b0), .CP_u(clk), .clr(or_1_out), .QD(\四位二进制带同步加载的可逆计数器_1_qd ), .QB(\四位二进制带同步加载的可逆计数器_1_qb ),
    .QA(\四位二进制带同步加载的可逆计数器_1_qa ), .ld_3(1'b0), .ld(1'b0), .ld_2(1'b0), .ld_1(1'b0), .ld_0(1'b0));  // open: QC
  or or_2 (or_2_out, clr, change);
  and and_2 (and_2_out, \四位二进制带同步加载的可逆计数器_1_qb , \四位二进制带同步加载的可逆计数器_1_qa );
  \四位二进制带同步加载的可逆计数器  \u_四位二进制带同步加载的可逆计数器_2  (
    .CP_d(1'b0), .CP_u(and_1_out), .clr(or_2_out), .QB(\四位二进制带同步加载的可逆计数器_2_qb ),
    .QA(\四位二进制带同步加载的可逆计数器_2_qa ), .ld_3(1'b0), .ld(1'b0), .ld_2(1'b0), .ld_1(1'b0), .ld_0(1'b0));  // open: QD, QC

  // Notes on the sheet:
  //   mod10
  //   3s
  //   20s
  //   10s
endmodule

module \主控电路  (
  input  clk,
  input  clr,
  input  button_else,
  input  button_main,
  output X1,
  output X0
);

  wire and_1_out, and_2_out, nor_1_out, not_1_out, not_2_out, not_3_out, not_4_out, or_1_out, or_2_out,
       or_3_out, \四位二进制带同步加载的可逆计数器_1_qc ;

  or or_1 (or_1_out, \四位二进制带同步加载的可逆计数器_1_qc , clr);
  not not_1 (not_1_out, button_else);
  or or_2 (or_2_out, not_1_out, not_1_out);
  nor nor_1 (nor_1_out, button_else, button_main);
  and and_1 (and_1_out, button_else, not_4_out, not_3_out);
  and and_2 (and_2_out, button_main, X1, not_4_out);
  \四位二进制带同步加载的可逆计数器  \u_四位二进制带同步加载的可逆计数器_1  (
    .CP_d(1'b0), .CP_u(clk), .clr(or_1_out), .QC(\四位二进制带同步加载的可逆计数器_1_qc ), .QB(X1), .QA(X0), .ld_3(1'b0),
    .ld(or_3_out), .ld_2(1'b0), .ld_1(or_2_out), .ld_0(not_2_out));  // open: QD
  not not_2 (not_2_out, nor_1_out);
  or or_3 (or_3_out, and_1_out, and_2_out);
  not not_3 (not_3_out, X1);
  not not_4 (not_4_out, X0);
endmodule

module \信号灯译码驱动电路  (
  input  X1,
  input  clk,
  input  X0,
  output out_4,
  output out_5,
  output out_6,
  output out_7,
  output out_8,
  output out_9
);

  wire and_1_out, and_3_out, not_2_out;

  not not_1 (out_7, X1);
  not not_2 (not_2_out, X0);
  and and_1 (and_1_out, X0, out_7);
  and and_2 (out_6, out_7, not_2_out);
  and and_3 (and_3_out, X0, X1);
  and and_4 (out_9, X1, not_2_out);
  and and_5 (out_5, and_1_out, clk);
  and and_6 (out_8, clk, and_3_out);
  LED M_R (.in(X1));
  LED M_Y (.in(out_5));
  LED M_G (.in(out_6));
  LED E_R (.in(out_7));
  LED E_Y (.in(out_8));
  LED E_G (.in(out_9));

  assign out_4 = X1;
endmodule

module \区别主支干道且带行人检测的交通信号灯电路  (
  input  \else通行 ,
  input  \main通行 ,
  input  clr,
  input  clk,
  output mainR,
  output mainY,
  output mainG,
  output esleR,
  output elseY,
  output elseG
);

  wire or_1_out, \主控电路_1_x0 , \主控电路_1_x1 , \红绿灯点亮时长计时器_1_change ;

  or or_1 (or_1_out, \else通行 , \main通行 , clr);
  \主控电路  \u_主控电路_1  (
    .clk(\红绿灯点亮时长计时器_1_change ), .X1(\主控电路_1_x1 ), .X0(\主控电路_1_x0 ), .button_else(\else通行 ),
    .button_main(\main通行 ), .clr(clr));
  \红绿灯点亮时长计时器  \u_红绿灯点亮时长计时器_1  (
    .clr(or_1_out), .X0(\主控电路_1_x0 ), .X1(\主控电路_1_x1 ), .change(\红绿灯点亮时长计时器_1_change ), .clk(clk));
  \信号灯译码驱动电路  \u_信号灯译码驱动电路_1  (
    .X1(\主控电路_1_x1 ), .clk(clk), .X0(\主控电路_1_x0 ), .out_4(mainR), .out_5(mainY), .out_6(mainG),
    .out_7(esleR), .out_8(elseY), .out_9(elseG));
  LED led_1 (.in(esleR));
  LED led_2 (.in(elseY));
  LED led_3 (.in(elseG));
  LED led_4 (.in(mainG));
  LED led_5 (.in(mainR));
  LED led_6 (.in(mainY));
endmodule

module \封装后的交通信号灯电路  (
);

  wire button_1_out, button_2_out, button_3_out, clock_1_out, \区别主支干道且带行人检测的交通信号灯电路_1_elseg ,
       \区别主支干道且带行人检测的交通信号灯电路_1_elsey , \区别主支干道且带行人检测的交通信号灯电路_1_esler , \区别主支干道且带行人检测的交通信号灯电路_1_maing ,
       \区别主支干道且带行人检测的交通信号灯电路_1_mainr , \区别主支干道且带行人检测的交通信号灯电路_1_mainy ;

  Button button_1 (.out(button_1_out));
  Button button_2 (.out(button_2_out));
  Button button_3 (.out(button_3_out));
  Clock clock_1 (.out(clock_1_out));
  \区别主支干道且带行人检测的交通信号灯电路  \u_区别主支干道且带行人检测的交通信号灯电路_1  (
    .clr(button_3_out), .clk(clock_1_out), .mainR(\区别主支干道且带行人检测的交通信号灯电路_1_mainr ),
    .mainY(\区别主支干道且带行人检测的交通信号灯电路_1_mainy ), .mainG(\区别主支干道且带行人检测的交通信号灯电路_1_maing ),
    .esleR(\区别主支干道且带行人检测的交通信号灯电路_1_esler ), .elseY(\区别主支干道且带行人检测的交通信号灯电路_1_elsey ),
    .elseG(\区别主支干道且带行人检测的交通信号灯电路_1_elseg ), .\else通行 (button_1_out), .\main通行 (button_2_out));
  LED led_1 (.in(\区别主支干道且带行人检测的交通信号灯电路_1_elseg ));
  LED led_2 (.in(\区别主支干道且带行人检测的交通信号灯电路_1_elsey ));
  LED led_3 (.in(\区别主支干道且带行人检测的交通信号灯电路_1_esler ));
  LED led_4 (.in(\区别主支干道且带行人检测的交通信号灯电路_1_mainr ));
  LED led_5 (.in(\区别主支干道且带行人检测的交通信号灯电路_1_maing ));
  LED led_6 (.in(\区别主支干道且带行人检测的交通信号灯电路_1_mainy ));
  LED led_7 (.in(\区别主支干道且带行人检测的交通信号灯电路_1_maing ));
  LED led_8 (.in(\区别主支干道且带行人检测的交通信号灯电路_1_mainr ));
  LED led_9 (.in(\区别主支干道且带行人检测的交通信号灯电路_1_mainy ));
  LED led_10 (.in(\区别主支干道且带行人检测的交通信号灯电路_1_esler ));
  LED led_11 (.in(\区别主支干道且带行人检测的交通信号灯电路_1_elsey ));
  LED led_12 (.in(\区别主支干道且带行人检测的交通信号灯电路_1_elseg ));

  // Notes on the sheet:
  //   注：通过菜单中simulate->ticks enabled选项开启时钟以预览效果(建议frequency:4Hz/2Hz)
  //   支干道
  //   主干道
endmodule
