// Logisim project lab1.circ as structural Verilog
module \一位二进制半加器  (
  input  \输入A ,
  input  \输入B ,
  output \本位输出C ,
  output \进位输出S 
);

  xor xor_1 (\本位输出C , \输入A , \输入B );
  and and_1 (\进位输出S , \输入A , \输入B );

  // Notes on the sheet:
  //   一位二进制半加器
endmodule

module \一位二进制全加器  (
  input  \输入A ,
  input  \输入B ,
  input  \低位进位Ci ,
  output \本位输出S ,
  output \进位输出Co 
);

  wire and_1_out, and_2_out, xor_1_out;

  xor xor_1 (xor_1_out, \输入A , \输入B );
  and and_1 (and_1_out, \输入A , \输入B );
  xor xor_2 (\本位输出S , xor_1_out, \低位进位Ci );
  and and_2 (and_2_out, xor_1_out, \低位进位Ci );
  or or_1 (\进位输出Co , and_2_out, and_1_out);

  // Notes on the sheet:
  //   一位二进制全加器
endmodule

module \串行进位的四位二进制并行加法器  (
  input  A3,
  input  B3,
  input  A2,
  input  B2,
  input  A1,
  input  B1,
  input  A0,
  input  B0,
  input  C0,
  output C4,
  output S3,
  output S2,
  output S1,
  output S0
);

  wire \一位二进制全加器_2_进位输出co , \一位二进制全加器_3_进位输出co , \一位二进制全加器_4_进位输出co ;

  \一位二进制全加器  \u_一位二进制全加器_1  (.\输入A (A3), .\输入B (B3), .\低位进位Ci (\一位二进制全加器_2_进位输出co ), .\本位输出S (S3), .\进位输出Co (C4));
  \一位二进制全加器  \u_一位二进制全加器_2  (
    .\输入A (A2), .\输入B (B2), .\低位进位Ci (\一位二进制全加器_3_进位输出co ), .\本位输出S (S2), .\进位输出Co (\一位二进制全加器_2_进位输出co ));
  \一位二进制全加器  \u_一位二进制全加器_3  (
    .\输入A (A1), .\输入B (B1), .\低位进位Ci (\一位二进制全加器_4_进位输出co ), .\本位输出S (S1), .\进位输出Co (\一位二进制全加器_3_进位输出co ));
  \一位二进制全加器  \u_一位二进制全加器_4  (.\输入A (A0), .\输入B (B0), .\低位进位Ci (C0), .\本位输出S (S0), .\进位输出Co (\一位二进制全加器_4_进位输出co ));

  // Notes on the sheet:
  //   串行进位的四位二进制并行加法器
endmodule

module \先行进位的四位二进制并行加法器  (
  input  A3,
  input  B3,
  input  A2,
  input  B2,
  input  A1,
  input  B1,
  input  A0,
  input  B0,
  input  C0,
  output C4,
  output S3,
  output S2,
  output S1,
  output S0
);

  wire and_1_out, and_2_out, and_3_out, and_4_out, and_5_out, and_6_out, and_7_out, and_8_out, and_9_out,
       and_10_out, C1_out, C2_out, C3_out, G0_out, G1_out, G2_out, G3_out, P0_out, P1_out, P2_out, P3_out;

  and G3 (G3_out, A3, B3);
  and G2 (G2_out, A2, B2);
  and G1 (G1_out, A1, B1);
  and G0 (G0_out, A0, B0);
  xor P3 (P3_out, A3, B3);
  xor P2 (P2_out, A2, B2);
  xor P1 (P1_out, A1, B1);
  xor P0 (P0_out, A0, B0);
  and and_1 (and_1_out, P3_out, P2_out, P1_out, P0_out, C0);
  and and_2 (and_2_out, P3_out, P2_out, P1_out, G0_out);
  and and_3 (and_3_out, P3_out, P2_out, G1_out);
  and and_4 (and_4_out, P3_out, G2_out);
  and and_5 (and_5_out, P2_out, P1_out, P0_out, C0);
  and and_6 (and_6_out, P2_out, P1_out, G0_out);
  and and_7 (and_7_out, P2_out, G1_out);
  and and_8 (and_8_out, P1_out, P0_out, C0);
  and and_9 (and_9_out, P1_out, G0_out);
  and and_10 (and_10_out, P0_out, C0);
  or u_C4 (C4, G3_out, and_1_out, and_2_out, and_3_out, and_4_out);
  or C3 (C3_out, and_5_out, and_6_out, and_7_out, G2_out);
  or C2 (C2_out, and_8_out, and_9_out, G1_out);
  or C1 (C1_out, G0_out, and_10_out);
  \一位二进制全加器  \u_一位二进制全加器_1  (.\输入A (A3), .\输入B (B3), .\低位进位Ci (C3_out), .\本位输出S (S3));  // open: 进位输出Co
  \一位二进制全加器  \u_一位二进制全加器_2  (.\输入A (A2), .\输入B (B2), .\低位进位Ci (C2_out), .\本位输出S (S2));  // open: 进位输出Co
  \一位二进制全加器  \u_一位二进制全加器_3  (.\输入A (A1), .\输入B (B1), .\低位进位Ci (C1_out), .\本位输出S (S1));  // open: 进位输出Co
  \一位二进制全加器  \u_一位二进制全加器_4  (.\输入A (A0), .\输入B (B0), .\低位进位Ci (C0), .\本位输出S (S0));  // open: 进位输出Co

  // Notes on the sheet:
  //   先行进位的四位二进制并行加法器
  //   C4=P3P2P1P0C0+P3P2P1G0+P3P2G1+P3G2+G3
  //    C2=P1P0C0+P1G0+G1
  //   C1=P0C0+G0
  //   C3=P2P1P0C0+P2P1G0+P2G1+G2 
endmodule

module \将先行进位的四位二进制并行加法器封装成一个组件  (
  input  A3,
  input  A2,
  input  A1,
  input  A0,
  input  B3,
  input  B2,
  input  B1,
  input  B0,
  input  C0,
  output C4,
  output S3,
  output S2,
  output S1,
  output S0
);

  \先行进位的四位二进制并行加法器  \u_先行进位的四位二进制并行加法器_1  (
    .A3(A3), .B3(B3), .A2(A2), .B2(B2), .A1(A1), .B1(B1), .A0(A0), .B0(B0), .C0(C0), .C4(C4), .S3(S3),
    .S2(S2), .S1(S1), .S0(S0));

  // Notes on the sheet:
  //   先行进位四位二进制并行加法器测试电路
endmodule
