// Logisim project lab2.circ as structural Verilog
module \一位二进制全加器  (
  input  A,
  input  B,
  input  Ci,
  output S,
  output Co
);

  wire and_1_out, and_2_out, xor_1_out;

  xor xor_1 (xor_1_out, A, B);
  and and_1 (and_1_out, A, B);
  xor xor_2 (S, xor_1_out, Ci);
  and and_2 (and_2_out, xor_1_out, Ci);
  or or_1 (Co, and_2_out, and_1_out);
endmodule

module \先行进位的四位二进制并行加法器  (
  input  A3,
  input  B3,
  input  A2,
  input  B2,
  input  A1,
  input  B1,
  input  A0,
  input  B0,
  input  C0,
  output C4,
  output S3,
  output S2,
  output S1,
  output S0
);

  wire and_1_out, and_2_out, and_3_out, and_4_out, and_5_out, and_6_out, and_7_out, and_8_out, and_9_out,
       and_10_out, C1_out, C2_out, C3_out, G0_out, G1_out, G2_out, G3_out, P0_out, P1_out, P2_out, P3_out;

  and G3 (G3_out, A3, B3);
  and G2 (G2_out, A2, B2);
  and G1 (G1_out, A1, B1);
  and G0 (G0_out, A0, B0);
  xor P3 (P3_out, A3, B3);
  xor P2 (P2_out, A2, B2);
  xor P1 (P1_out, A1, B1);
  xor P0 (P0_out, A0, B0);
  and and_1 (and_1_out, P3_out, P2_out, P1_out, P0_out, C0);
  and and_2 (and_2_out, P3_out, P2_out, P1_out, G0_out);
  and and_3 (and_3_out, P3_out, P2_out, G1_out);
  and and_4 (and_4_out, P3_out, G2_out);
  and and_5 (and_5_out, P2_out, P1_out, P0_out, C0);
  and and_6 (and_6_out, P2_out, P1_out, G0_out);
  and and_7 (and_7_out, P2_out, G1_out);
  and and_8 (and_8_out, P1_out, P0_out, C0);
  and and_9 (and_9_out, P1_out, G0_out);
  and and_10 (and_10_out, P0_out, C0);
  or u_C4 (C4, G3_out, and_1_out, and_2_out, and_3_out, and_4_out);
  or C3 (C3_out, and_5_out, and_6_out, and_7_out, G2_out);
  or C2 (C2_out, and_8_out, and_9_out, G1_out);
  or C1 (C1_out, G0_out, and_10_out);
  \一位二进制全加器  \u_一位二进制全加器_1  (.A(A3), .B(B3), .Ci(C3_out), .S(S3));  // open: Co
  \一位二进制全加器  \u_一位二进制全加器_2  (.A(A2), .B(B2), .Ci(C2_out), .S(S2));  // open: Co
  \一位二进制全加器  \u_一位二进制全加器_3  (.A(A1), .B(B1), .Ci(C1_out), .S(S1));  // open: Co
  \一位二进制全加器  \u_一位二进制全加器_4  (.A(A0), .B(B0), .Ci(C0), .S(S0));  // open: Co

  // Notes on the sheet:
  //   C4=P3P2P1P0C0+P3P2P1G0+P3P2G1+P3G2+G3
  //    C2=P1P0C0+P1G0+G1
  //   C1=P0C0+G0
  //   C3=P2P1P0C0+P2P1G0+P2G1+G2 
endmodule

module \四位二进制可逆计数器  (
  input  CP_d,
  input  CP_u,
  input  clr,
  output QD,
  output QC,
  output QB,
  output QA
);

  wire and_1_out, and_2_out, and_3_out, and_4_out, and_5_out, and_6_out, and_7_out, and_8_out, and_9_out,
       and_10_out, D0_qn, D1_qn, D2_qn, or_1_out, or_2_out, or_3_out, or_4_out, or_5_out, or_6_out, or_7_out,
       xor_1_out, xor_2_out, xor_3_out, xor_4_out, xor_5_out, xor_6_out;

  and and_1 (and_1_out, QC, QB, QA);
  and and_2 (and_2_out, D2_qn, D1_qn, D0_qn);
  and and_3 (and_3_out, QB, QA);
  and and_4 (and_4_out, D1_qn, D0_qn);
  xor xor_1 (xor_1_out, and_1_out, QD);
  xor xor_2 (xor_2_out, and_2_out, QD);
  xor xor_3 (xor_3_out, and_3_out, QC);
  xor xor_4 (xor_4_out, and_4_out, QC);
  xor xor_5 (xor_5_out, QB, QA);
  xor xor_6 (xor_6_out, D0_qn, QB);
  and and_5 (and_5_out, CP_u, xor_1_out);
  and and_6 (and_6_out, CP_d, xor_2_out);
  and and_7 (and_7_out, CP_u, xor_3_out);
  and and_8 (and_8_out, CP_d, xor_4_out);
  and and_9 (and_9_out, CP_u, xor_5_out);
  and and_10 (and_10_out, CP_d, xor_6_out);
  or or_1 (or_1_out, CP_u, CP_d);
  D_Flip_Flop #(.trigger("falling")) D3 (.clk(or_1_out), .D(or_2_out), .Q(QD), .reset(clr));  // open: Qn, preset, en
  or or_2 (or_2_out, and_5_out, and_6_out);
  or or_3 (or_3_out, CP_u, CP_d);
  D_Flip_Flop #(.trigger("falling")) D2 (
    .clk(or_3_out), .D(or_4_out), .Q(QC), .Qn(D2_qn), .reset(clr));  // open: preset, en
  or or_4 (or_4_out, and_7_out, and_8_out);
  D_Flip_Flop #(.trigger("falling")) D1 (
    .clk(or_5_out), .D(or_6_out), .Q(QB), .Qn(D1_qn), .reset(clr));  // open: preset, en
  or or_5 (or_5_out, CP_u, CP_d);
  or or_6 (or_6_out, and_9_out, and_10_out);
  or or_7 (or_7_out, CP_u, CP_d);
  D_Flip_Flop #(.trigger("falling")) D0 (
    .clk(or_7_out), .D(D0_qn), .Q(QA), .Qn(D0_qn), .reset(clr));  // open: preset, en
endmodule

module \将实验室内人数转换成8421BCD码的电路  (
  input  QD,
  input  QC,
  input  QB,
  input  QA,
  output D10,
  output D03,
  output D02,
  output D01,
  output D00
);

  wire nand_1_out, nand_2_out, not_1_out;

  not not_1 (not_1_out, 1'b1);
  \先行进位的四位二进制并行加法器  \u_先行进位的四位二进制并行加法器_1  (
    .A3(QD), .B3(not_1_out), .A2(QC), .B2(D10), .A1(QB), .B1(D10), .A0(QA), .B0(not_1_out), .C0(not_1_out),
    .S3(D03), .S2(D02), .S1(D01), .S0(D00));  // open: C4
  nand nand_1 (nand_1_out, QD, QC);
  nand nand_2 (nand_2_out, QD, QB);
  nand nand_3 (D10, nand_1_out, nand_2_out);
endmodule

module \_7段译码器  (
  input  a3,
  input  a2,
  input  a1,
  input  a0,
  output a,
  output b,
  output c,
  output d,
  output e,
  output f,
  output g
);

  wire a1_a0_out, a1a0_out, a2_a0_out, a2_a1_out, a2_a1a0_out, a2a0_out, a_out, and_1_out, b_out, c_out,
       d_out, e_out, f_out, g_out, na1_a0_out, na2_a0_out, na2a1_out, nand_1_out, nand_2_out, not_1_out,
       not_2_out, not_3_out;

  not not_1 (not_1_out, a2);
  not not_2 (not_2_out, a1);
  not not_3 (not_3_out, a0);
  and na2_a0 (na2_a0_out, not_1_out, not_3_out);
  and a2a0 (a2a0_out, a2, a0);
  and na2a1 (na2a1_out, not_1_out, a1);
  and na1_a0 (na1_a0_out, not_2_out, not_3_out);
  and a1a0 (a1a0_out, a1, a0);
  and a1_a0 (a1_a0_out, a1, not_3_out);
  and a2_a1a0 (a2_a1a0_out, a2, not_2_out, a0);
  and a2_a1 (a2_a1_out, a2, not_2_out);
  and a2_a0 (a2_a0_out, a2, not_3_out);
  nand nand_1 (nand_1_out, a3, a2);
  and and_1 (and_1_out, nand_1_out, nand_2_out);
  nand nand_2 (nand_2_out, a3, a1);
  or u_a (a_out, na2_a0_out, a2a0_out, na2a1_out, a3);
  or u_b (b_out, na1_a0_out, a1a0_out, not_1_out);
  or u_c (c_out, not_2_out, a0, a2);
  or u_d (d_out, na2_a0_out, a1_a0_out, na2a1_out, a2_a1a0_out);
  or u_e (e_out, na2_a0_out, a1_a0_out);
  or u_f (f_out, na1_a0_out, a2_a1_out, a2_a0_out, a3);
  or u_g (g_out, na2a1_out, a2_a1_out, a1_a0_out, a3);
  and and_2 (a, a_out, and_1_out);
  and and_3 (b, b_out, and_1_out);
  and and_4 (c, c_out, and_1_out);
  and and_5 (d, d_out, and_1_out);
  and and_6 (e, e_out, and_1_out);
  and and_7 (f, f_out, and_1_out);
  and and_8 (g, g_out, and_1_out);
endmodule

module \_7段译码器显示人数  (
  input  QD,
  input  QC,
  input  QB,
  input  QA
);

  wire \n7段译码器_1_a , \n7段译码器_1_b , \n7段译码器_1_c , \n7段译码器_1_d , \n7段译码器_1_e , \n7段译码器_1_f , \n7段译码器_1_g ,
       \n7段译码器_2_a , \n7段译码器_2_b , \n7段译码器_2_c , \n7段译码器_2_d , \n7段译码器_2_e , \n7段译码器_2_f , \n7段译码器_2_g ,
       not_1_out, \将实验室内人数转换成8421bcd码的电路_1_d00 , \将实验室内人数转换成8421bcd码的电路_1_d01 ,
       \将实验室内人数转换成8421bcd码的电路_1_d02 , \将实验室内人数转换成8421bcd码的电路_1_d03 , \将实验室内人数转换成8421bcd码的电路_1_d10 ;

  not not_1 (not_1_out, 1'b1);
  \将实验室内人数转换成8421BCD码的电路  \u_将实验室内人数转换成8421bcd码的电路_1  (
    .QD(QD), .QC(QC), .QB(QB), .QA(QA), .D10(\将实验室内人数转换成8421bcd码的电路_1_d10 ),
    .D03(\将实验室内人数转换成8421bcd码的电路_1_d03 ), .D02(\将实验室内人数转换成8421bcd码的电路_1_d02 ),
    .D01(\将实验室内人数转换成8421bcd码的电路_1_d01 ), .D00(\将实验室内人数转换成8421bcd码的电路_1_d00 ));
  \_7段译码器  \u_7段译码器_1  (
    .a3(not_1_out), .a2(not_1_out), .a1(not_1_out), .a0(\将实验室内人数转换成8421bcd码的电路_1_d10 ), .a(\n7段译码器_1_a ),
    .b(\n7段译码器_1_b ), .c(\n7段译码器_1_c ), .d(\n7段译码器_1_d ), .e(\n7段译码器_1_e ), .f(\n7段译码器_1_f ), .g(\n7段译码器_1_g ));
  \_7段译码器  \u_7段译码器_2  (
    .a3(\将实验室内人数转换成8421bcd码的电路_1_d03 ), .a2(\将实验室内人数转换成8421bcd码的电路_1_d02 ),
    .a1(\将实验室内人数转换成8421bcd码的电路_1_d01 ), .a0(\将实验室内人数转换成8421bcd码的电路_1_d00 ), .a(\n7段译码器_2_a ),
    .b(\n7段译码器_2_b ), .c(\n7段译码器_2_c ), .d(\n7段译码器_2_d ), .e(\n7段译码器_2_e ), .f(\n7段译码器_2_f ), .g(\n7段译码器_2_g ));
  _7_Segment_Display u_7_segment_display_1 (
    .g(\n7段译码器_2_g ), .f(\n7段译码器_2_f ), .a(\n7段译码器_2_a ), .b(\n7段译码器_2_b ), .e(\n7段译码器_2_e ),
    .d(\n7段译码器_2_d ), .c(\n7段译码器_2_c ));  // open: dp
  _7_Segment_Display u_7_segment_display_2 (
    .g(\n7段译码器_1_g ), .f(\n7段译码器_1_f ), .a(\n7段译码器_1_a ), .b(\n7段译码器_1_b ), .e(\n7段译码器_1_e ),
    .d(\n7段译码器_1_d ), .c(\n7段译码器_1_c ));  // open: dp
endmodule

module \满员报警的四位二进制可逆计数器  (
  input  CP_u,
  input  clr,
  input  CP_d,
  output QD,
  output QC,
  output QB,
  output QA,
  output ALARM
);

  wire and_1_out, and_2_out, nand_1_out, or_1_out;

  and and_1 (and_1_out, nand_1_out, CP_u);
  and and_2 (and_2_out, CP_d, or_1_out);
  \四位二进制可逆计数器  \u_四位二进制可逆计数器_1  (.CP_d(and_2_out), .CP_u(and_1_out), .clr(clr), .QD(QD), .QC(QC), .QB(QB), .QA(QA));
  and and_3 (ALARM, QA, QB, QC, QD, CP_u);
  nand nand_1 (nand_1_out, QA, QB, QC, QD);
  or or_1 (or_1_out, QA, QB, QC, QD);
endmodule

module \小型实验室门禁系统电路  (
  input  in_1,
  input  in_2,
  input  in_3,
  output out_4,
  output out_5,
  output out_6,
  output out_7,
  output out_8,
  output out_9,
  output out_10,
  output out_11,
  output out_12,
  output out_13,
  output out_14,
  output out_15,
  output out_16,
  output out_17,
  output out_18
);

  wire not_1_out, \将实验室内人数转换成8421bcd码的电路_1_d00 , \将实验室内人数转换成8421bcd码的电路_1_d01 ,
       \将实验室内人数转换成8421bcd码的电路_1_d02 , \将实验室内人数转换成8421bcd码的电路_1_d03 , \将实验室内人数转换成8421bcd码的电路_1_d10 ,
       \满员报警的四位二进制可逆计数器_1_qa , \满员报警的四位二进制可逆计数器_1_qb , \满员报警的四位二进制可逆计数器_1_qc , \满员报警的四位二进制可逆计数器_1_qd ;

  not not_1 (not_1_out, 1'b1);
  \将实验室内人数转换成8421BCD码的电路  \u_将实验室内人数转换成8421bcd码的电路_1  (
    .QD(\满员报警的四位二进制可逆计数器_1_qd ), .QC(\满员报警的四位二进制可逆计数器_1_qc ), .QB(\满员报警的四位二进制可逆计数器_1_qb ),
    .QA(\满员报警的四位二进制可逆计数器_1_qa ), .D10(\将实验室内人数转换成8421bcd码的电路_1_d10 ), .D03(\将实验室内人数转换成8421bcd码的电路_1_d03 ),
    .D02(\将实验室内人数转换成8421bcd码的电路_1_d02 ), .D01(\将实验室内人数转换成8421bcd码的电路_1_d01 ),
    .D00(\将实验室内人数转换成8421bcd码的电路_1_d00 ));
  \满员报警的四位二进制可逆计数器  \u_满员报警的四位二进制可逆计数器_1  (
    .QD(\满员报警的四位二进制可逆计数器_1_qd ), .QC(\满员报警的四位二进制可逆计数器_1_qc ), .QB(\满员报警的四位二进制可逆计数器_1_qb ),
    .QA(\满员报警的四位二进制可逆计数器_1_qa ), .ALARM(out_18), .CP_d(in_3), .CP_u(in_1), .clr(in_2));
  \_7段译码器  \u_7段译码器_1  (
    .a3(not_1_out), .a2(not_1_out), .a1(not_1_out), .a0(\将实验室内人数转换成8421bcd码的电路_1_d10 ), .a(out_4), .b(out_5),
    .c(out_6), .d(out_7), .e(out_8), .f(out_9), .g(out_10));
  \_7段译码器  \u_7段译码器_2  (
    .a3(\将实验室内人数转换成8421bcd码的电路_1_d03 ), .a2(\将实验室内人数转换成8421bcd码的电路_1_d02 ),
    .a1(\将实验室内人数转换成8421bcd码的电路_1_d01 ), .a0(\将实验室内人数转换成8421bcd码的电路_1_d00 ), .a(out_11), .b(out_12),
    .c(out_13), .d(out_14), .e(out_15), .f(out_16), .g(out_17));
  _7_Segment_Display u_7_segment_display_1 (
    .g(out_10), .f(out_9), .a(out_4), .b(out_5), .e(out_8), .d(out_7), .c(out_6));  // open: dp
  _7_Segment_Display u_7_segment_display_2 (
    .g(out_17), .f(out_16), .a(out_11), .b(out_12), .e(out_15), .d(out_14), .c(out_13));  // open: dp
endmodule

module \封装后的小型实验室门禁系统电路  (
);

  wire CLR_out, CP_D_out, CP_U_out, \小型实验室门禁系统电路_1_out_4 , \小型实验室门禁系统电路_1_out_5 , \小型实验室门禁系统电路_1_out_6 ,
       \小型实验室门禁系统电路_1_out_7 , \小型实验室门禁系统电路_1_out_8 , \小型实验室门禁系统电路_1_out_9 , \小型实验室门禁系统电路_1_out_10 ,
       \小型实验室门禁系统电路_1_out_11 , \小型实验室门禁系统电路_1_out_12 , \小型实验室门禁系统电路_1_out_13 , \小型实验室门禁系统电路_1_out_14 ,
       \小型实验室门禁系统电路_1_out_15 , \小型实验室门禁系统电路_1_out_16 , \小型实验室门禁系统电路_1_out_17 , \小型实验室门禁系统电路_1_out_18 ;

  Button CP_U (.out(CP_U_out));
  Button CLR (.out(CLR_out));
  Button CP_D (.out(CP_D_out));
  \小型实验室门禁系统电路  \u_小型实验室门禁系统电路_1  (
    .in_1(CP_U_out), .in_2(CLR_out), .in_3(CP_D_out), .out_4(\小型实验室门禁系统电路_1_out_4 ),
    .out_5(\小型实验室门禁系统电路_1_out_5 ), .out_6(\小型实验室门禁系统电路_1_out_6 ), .out_7(\小型实验室门禁系统电路_1_out_7 ),
    .out_8(\小型实验室门禁系统电路_1_out_8 ), .out_9(\小型实验室门禁系统电路_1_out_9 ), .out_10(\小型实验室门禁系统电路_1_out_10 ),
    .out_11(\小型实验室门禁系统电路_1_out_11 ), .out_12(\小型实验室门禁系统电路_1_out_12 ), .out_13(\小型实验室门禁系统电路_1_out_13 ),
    .out_14(\小型实验室门禁系统电路_1_out_14 ), .out_15(\小型实验室门禁系统电路_1_out_15 ), .out_16(\小型实验室门禁系统电路_1_out_16 ),
    .out_17(\小型实验室门禁系统电路_1_out_17 ), .out_18(\小型实验室门禁系统电路_1_out_18 ));
  _7_Segment_Display u_7_segment_display_1 (
    .g(\小型实验室门禁系统电路_1_out_17 ), .f(\小型实验室门禁系统电路_1_out_16 ), .a(\小型实验室门禁系统电路_1_out_11 ),
    .b(\小型实验室门禁系统电路_1_out_12 ), .e(\小型实验室门禁系统电路_1_out_15 ), .d(\小型实验室门禁系统电路_1_out_14 ),
    .c(\小型实验室门禁系统电路_1_out_13 ));  // open: dp
  _7_Segment_Display u_7_segment_display_2 (
    .g(\小型实验室门禁系统电路_1_out_10 ), .f(\小型实验室门禁系统电路_1_out_9 ), .a(\小型实验室门禁系统电路_1_out_4 ),
    .b(\小型实验室门禁系统电路_1_out_5 ), .e(\小型实验室门禁系统电路_1_out_8 ), .d(\小型实验室门禁系统电路_1_out_7 ), .c(\小型实验室门禁系统电路_1_out_6 ));  // open: dp
  LED ALARM (.in(\小型实验室门禁系统电路_1_out_18 ));
endmodule
