// Logisim project T5.15.circ as structural Verilog: 1 circuit, main circuit main
module main (
  input  \置1_高电平有效 ,
  input  \置0_高电平有效 
);

  wire and_1_out, and_2_out, and_3_out, and_4_out, CP_out, or_1_out, T1_q, T2_q, T3_q, T4_q, T4_qn;

  and and_1 (and_1_out, T4_q, T1_q);
  and and_2 (and_2_out, T1_q, T2_q, T3_q);
  Button CP (.out(CP_out));
  or or_1 (or_1_out, and_1_out, and_2_out);
  and and_3 (and_3_out, T2_q, T1_q);
  and and_4 (and_4_out, T4_qn, T1_q);
  T_Flip_Flop T4 (
    .clk(CP_out), .T(or_1_out), .Q(T4_q), .Qn(T4_qn), .preset(\置1_高电平有效 ), .reset(\置0_高电平有效 ));  // open: en
  T_Flip_Flop T3 (.clk(CP_out), .T(and_3_out), .Q(T3_q), .preset(\置1_高电平有效 ), .reset(\置0_高电平有效 ));  // open: Qn, en
  T_Flip_Flop T2 (.clk(CP_out), .T(and_4_out), .Q(T2_q), .preset(\置1_高电平有效 ), .reset(\置0_高电平有效 ));  // open: Qn, en
  T_Flip_Flop T1 (.clk(CP_out), .T(1'b1), .Q(T1_q), .preset(\置1_高电平有效 ), .reset(\置0_高电平有效 ));  // open: Qn, en
  LED y4 (.in(T4_q));
  LED y3 (.in(T3_q));
  LED y2 (.in(T2_q));
  LED y1 (.in(T1_q));

  // Notes on the sheet:
  //   题5.15  8421码十进制加一计数器
  //   计数循环：0000->0001
  //   ->0000
  //   ->0010->0011
  //   ->0100->0101
  //   ->0110->0111
  //   ->1000->1001
  //   8421码的其余六种无效状态会回到计数状态中
endmodule
