// Logisim project T5.5.circ as structural Verilog: 1 circuit, main circuit main
module main (
  input  \输入x 
);

  wire and_1_out, and_2_out, and_3_out, and_4_out, CP_out, D1_q, D1_qn, D2_q, D2_qn, nand_1_out, not_1_out,
       or_1_out, xor_1_out, xor_2_out;

  Button CP (.out(CP_out));
  D_Flip_Flop D2 (.clk(CP_out), .D(or_1_out), .Q(D2_q), .Qn(D2_qn));  // open: preset, en, reset
  or or_1 (or_1_out, and_1_out, and_2_out);
  and and_1 (and_1_out, \输入x , D1_qn);
  not not_1 (not_1_out, \输入x );
  LED y2 (.in(D2_q));
  and and_2 (and_2_out, not_1_out, D1_q, D2_qn);
  nand nand_1 (nand_1_out, D1_q, xor_1_out);
  LED y1 (.in(D1_q));
  D_Flip_Flop D1 (.clk(CP_out), .D(nand_1_out), .Q(D1_q), .Qn(D1_qn));  // open: preset, en, reset
  xor xor_1 (xor_1_out, D2_q, \输入x );
  and and_3 (and_3_out, D2_q, D1_q, not_1_out);
  // Probe on xor_2_out
  xor xor_2 (xor_2_out, and_3_out, and_4_out);
  and and_4 (and_4_out, D1_qn, D2_qn, \输入x );

  // Notes on the sheet:
  //   题5.5  模3可逆计数器(x=0时加计数 x=1时减计数)
  //   计数循环(x=0)：00->01->11->00
  //   计数循环(x=1)：00->11->10->00
endmodule
