// Logisim project 6.2.circ as structural Verilog: 1 circuit, main circuit main
module main (
  input  \置1_高电平有效 ,
  input  \置0_高电平有效 ,
  output \输出Z 
);

  wire _1_q, _1_qn, _2_q, _2_qn, and_1_out, and_2_out, and_3_out, not_1_out, or_1_out, or_2_out, or_3_out,
       x1_out, x2_out, x3_out;

  Button x1 (.out(x1_out));
  Button x2 (.out(x2_out));
  Button x3 (.out(x3_out));
  or or_1 (or_1_out, x3_out, x2_out, x1_out);
  and and_1 (and_1_out, x3_out, _1_qn);
  and and_2 (and_2_out, x2_out, _2_q);
  not not_1 (not_1_out, or_1_out);
  and and_3 (and_3_out, _2_qn, _1_q, x2_out);
  or or_2 (or_2_out, and_2_out, and_1_out, x1_out);
  or or_3 (or_3_out, and_2_out, x3_out);
  S_R_Flip_Flop #(.trigger("falling")) _2 (
    .S(and_3_out), .clk(not_1_out), .R(or_2_out), .Q(_2_q), .Qn(_2_qn), .preset(\置1_高电平有效 ),
    .reset(\置0_高电平有效 ));  // open: en
  S_R_Flip_Flop #(.trigger("falling")) _1 (
    .S(x1_out), .clk(not_1_out), .R(or_3_out), .Q(_1_q), .Qn(_1_qn), .preset(\置1_高电平有效 ), .reset(\置0_高电平有效 ));  // open: en
  LED Y2 (.in(_2_q));
  LED nY2 (.in(_2_qn));
  LED Y1 (.in(_1_q));
  LED nY1 (.in(_1_qn));
  and and_4 (\输出Z , _2_q, _1_qn);

  // Notes on the sheet:
  //   题6.2 "x1-x2-x3"序列检测器
  //   初始RS触发器输出y2y1为00
  //   顺序输入x1x2x3时y2y1依次为01-11-10
  //   输入x1时y2y1为01
  //    其余输入情况下y2y1均为00
  //   仅在顺序输入x1.x2.x3的脉冲时输出Z为1
endmodule
