// Logisim project 6.5.circ as structural Verilog: 1 circuit, main circuit 题6.5 八位序列检测器
module \题6_5_八位序列检测器  (
  output \输出Z 
);

  wire _1_q, _1_qn, _2_q, _2_qn, _3_q, _3_qn, and_1_out, x_out;

  Button x (.out(x_out));
  and and_1 (and_1_out, _1_qn, _2_qn);
  LED Y3 (.in(_3_q));
  D_Flip_Flop #(.trigger("falling")) _3 (.clk(and_1_out), .D(_3_qn), .Q(_3_q), .Qn(_3_qn));  // open: preset, en, reset
  LED Y2 (.in(_2_q));
  D_Flip_Flop #(.trigger("falling")) _2 (.clk(_1_qn), .D(_2_qn), .Q(_2_q), .Qn(_2_qn));  // open: preset, en, reset
  LED Y1 (.in(_1_q));
  D_Flip_Flop #(.trigger("falling")) _1 (.clk(x_out), .D(_1_qn), .Q(_1_q), .Qn(_1_qn));  // open: preset, en, reset
  and and_2 (\输出Z , _3_qn, _2_qn, _1_qn);

  // Notes on the sheet:
  //   题6.5 三位二进制减1计数器
  //   输入x脉冲时电路状态(Y3Y2Y1/Z)变化: 111/0->110/0->101/0->100/0
  //   ->011/0->010/0->001/0->000/1->111/0
endmodule
