// Logisim project CSIE1601_U201610504_刘逸帆_第四章电路设计.circ as structural Verilog: 1 circuit, main circuit main
module main (
  input  A,
  input  B,
  input  C,
  input  A_2,
  input  B_2,
  input  C_2,
  input  A_3,
  input  B_3,
  input  C_3,
  input  D
);

  wire nor_1_out, nor_2_out, nor_3_out, nor_4_out, nor_5_out, nor_6_out, nor_7_out, not_1_out, xnor_1_out,
       xor_1_out, xor_2_out, xor_3_out, xor_4_out;

  nor nor_1 (nor_1_out, A, B);
  nor nor_2 (nor_2_out, A, nor_1_out);
  nor nor_3 (nor_3_out, nor_1_out, B);
  xor xor_1 (xor_1_out, A_2, B_2);
  not not_1 (not_1_out, C_2);
  xor xor_2 (xor_2_out, A_3, B_3);
  xor xor_3 (xor_3_out, C_3, D);
  nor nor_4 (nor_4_out, nor_2_out, nor_3_out, C);
  nor nor_5 (nor_5_out, nor_3_out, nor_2_out, nor_4_out);
  nor nor_6 (nor_6_out, nor_4_out, C);
  // Probe on xor_4_out
  xor xor_4 (xor_4_out, xor_1_out, not_1_out);
  // Probe on xnor_1_out
  xnor xnor_1 (xnor_1_out, xor_2_out, xor_3_out);
  // Probe on nor_7_out
  nor nor_7 (nor_7_out, nor_5_out, nor_6_out);

  // Notes on the sheet:
  //   4.2 (1) 或非门实现的检测偶数个1输入的检测电路
  //   4.2 (2) 异或门实现的检测偶数个1输入的检测电路
  //   4.9异或门和异或非门实现的检测偶数个1输入的检测电路 
  //   F
  //   F
  //   F
endmodule
